// Logisim project Template.circ as structural Verilog: 4 circuits, main circuit main
module main (
  output [15:0] S
);

  wire clk, isbranch_1_s;
  wire [15:0] adder_1_out, isbranch_1_out_3, multiplexer_1_out, PC_q;

  // Text text_1: pin names not known
  // Text text_2: pin names not known
  // Text text_3: pin names not known
  // Text text_4: pin names not known
  // Text text_5: pin names not known
  Multiplexer #(.width(16), .enable("false")) multiplexer_1 (
    .in0(adder_1_out), .in1(isbranch_1_out_3), .out(multiplexer_1_out), .sel(isbranch_1_s));
  Clock #(.highDuration(4), .lowDuration(4)) u_clk (.out(clk));
  Clock sysclk ();  // open: out
  Register #(.width(16)) PC (.D(multiplexer_1_out), .clk(clk), .Q(PC_q));  // open: en, clr
  Adder #(.width(16)) adder_1 (.a(PC_q), .b(16'h2), .out(adder_1_out));  // open: cin, cout
  ROM #(.addrWidth(15), .dataWidth(16)) rom_1 (.addr(PC_q[15:1]), .data(S));
  isBranch isbranch_1 (.Current_Addr(PC_q), .E(S), .out_3(isbranch_1_out_3), .S(isbranch_1_s));

  // Notes on the sheet:
  //   LABO ARO 2 - FETCH
  //   HEIG-VD / Institut REDS
  //   Date : 25.02.2014
  //   Ne pas modifier les noms des clocks
  //   contents of rom_1 (hex, n*v repeats v):
  //   202a 2101 e014 21*0 2202 188b e7e4 1989*0 1
endmodule

module FETCH (
);

  // Text text_1: pin names not known
  // Text text_2: pin names not known
  // Text text_3: pin names not known
  // Text text_4: pin names not known
  // Text text_5: pin names not known
  D_Flip_Flop d_ff_1 ();  // open: clk, D, Q, Qn, preset, reset
endmodule

module PC_4BITS (
  input  [3:0] in_1,
  output [3:0] out_2
);

  wire CLK;

  // Text text_1: pin names not known
  // Text text_2: pin names not known
  // Text text_3: pin names not known
  // Text text_4: pin names not known
  // Text text_5: pin names not known
  Clock u_CLK (.out(CLK));
  D_Flip_Flop d_ff_1 (.D(in_1[0]), .clk(CLK), .Q(out_2[0]));  // open: Qn, preset, reset
  D_Flip_Flop d_ff_2 (.D(in_1[1]), .clk(CLK), .Q(out_2[1]));  // open: Qn, preset, reset
  D_Flip_Flop d_ff_3 (.D(in_1[2]), .clk(CLK), .Q(out_2[2]));  // open: Qn, preset, reset
  D_Flip_Flop d_ff_4 (.D(in_1[3]), .clk(CLK), .Q(out_2[3]));  // open: Qn, preset, reset
endmodule

module isBranch (
  input  [15:0] Current_Addr,
  input  [15:0] E,
  output [15:0] out_3,
  output S
);

  wire [15:0] adder_1_out, bit_extender_1_out, shifter_1_out;

  // Text text_1: pin names not known
  // Text text_2: pin names not known
  // Text text_3: pin names not known
  // Text text_4: pin names not known
  // Text text_5: pin names not known
  assign bit_extender_1_out = {{5{1'b0}}, E[10:0]};  // Bit_Extender bit_extender_1
  Comparator #(.width(5)) comparator_1 (.a(E[15:11]), .b(5'b11100), .eq(S));  // open: gt, lt
  Shifter #(.width(16)) shifter_1 (.in(bit_extender_1_out), .\dist (4'b0001), .out(shifter_1_out));
  Adder #(.width(16)) adder_1 (.a(Current_Addr), .b(shifter_1_out), .out(adder_1_out));  // open: cin, cout
  Adder #(.width(16)) adder_2 (.a(16'h4), .b(adder_1_out), .out(out_3));  // open: cin, cout

  // Notes on the sheet:
  //   TODO: complement à deux pourle déplacement en mémoire
endmodule
